// Logisim project 5.circ as structural Verilog: 1 circuit, main circuit main
module main (
  input  [7:0] NonMemoryInstructions,
  input  EnableCounter
);

  wire clock_1_out, Control_p2, Control_p3, Control_p4, Control_p5, Control_p6, Control_p7;
  wire [1:0] INSTRUCTION_MEMORY_PC_lsb, INSTRUCTION_MEMORY_PC_out_8, INSTRUCTION_MEMORY_PC_out_10,
       INSTRUCTION_MEMORY_PC_out_12, multiplexer_1_out;
  wire [3:0] ALU_p4, b_1_dataout, multiplexer_2_out, multiplexer_3_out, Registers_readdata1,
       Registers_readdata2;

  Q4B3_main INSTRUCTION_MEMORY_PC (
    .Reset(EnableCounter), .CLK(clock_1_out), .Data_In(NonMemoryInstructions), .RAM_Reset(1'b0),
    .MemWrite(1'b1), .Mem_Read_Write(1'b0), .MSB(INSTRUCTION_MEMORY_PC_out_8[1]),
    .out_8(INSTRUCTION_MEMORY_PC_out_8[0]), .out_9(INSTRUCTION_MEMORY_PC_out_10[1]),
    .out_10(INSTRUCTION_MEMORY_PC_out_10[0]), .out_11(INSTRUCTION_MEMORY_PC_out_12[1]),
    .out_12(INSTRUCTION_MEMORY_PC_out_12[0]), .out_13(INSTRUCTION_MEMORY_PC_lsb[1]),
    .LSB(INSTRUCTION_MEMORY_PC_lsb[0]));
  Clock clock_1 (.out(clock_1_out));
  Multiplexer #(.width(2), .enable("false")) multiplexer_1 (
    .in0(INSTRUCTION_MEMORY_PC_out_12), .in1(INSTRUCTION_MEMORY_PC_lsb), .out(multiplexer_1_out),
    .sel(Control_p2));
  // ControlTruth Control: pin names not known; wires that end beside it: INSTRUCTION_MEMORY_PC_out_8, Control_p2, Control_p3, Control_p4, Control_p5, Control_p6, Control_p7
  reg_file Registers (
    .WriteData(multiplexer_2_out), .WriteReg(multiplexer_1_out), .RegWrite(Control_p5), .Clock(clock_1_out),
    .ReadData1(Registers_readdata1), .ReadReg1(INSTRUCTION_MEMORY_PC_out_10),
    .ReadData2(Registers_readdata2), .ReadReg2(INSTRUCTION_MEMORY_PC_out_12));
  Multiplexer #(.width(4), .enable("false")) multiplexer_2 (
    .in0(ALU_p4), .in1(b_1_dataout), .out(multiplexer_2_out), .sel(Control_p4));
  Multiplexer #(.width(4), .enable("false")) multiplexer_3 (
    .in0(Registers_readdata2), .in1({2'b00, INSTRUCTION_MEMORY_PC_lsb}), .out(multiplexer_3_out),
    .sel(Control_p3));
  // ALU ALU: pin names not known; wires that end beside it: Registers_readdata1, multiplexer_3_out, Control_p7, ALU_p4
  b b_1 (
    .Address(Registers_readdata1), .Offset({2'b00, INSTRUCTION_MEMORY_PC_lsb}),
    .DataLoad(Registers_readdata2), .Store(Control_p6), .DataOut(b_1_dataout), .CLK(clock_1_out));

  // Notes on the sheet:
  //   OP
  //   RS
  //   RT
  //   RD/Offset
endmodule
